# Fritzing sketch POC Wiring (saved by Fritzing 0.9.4)
breadboards: 1

parts:
  Composant1 = Arduino Uno (Rev3)
  SG1 = Buzzer 12mm [package=buzzer-ccv-kit]
  R1 = Resistor [tolerance=±5% resistance=220 package="0402 [SMD]"]
  S1 = SWITCH-MOMENTARY-2 [package=tactile-pth-12mm]
  LED1 = LED - 3mm [color="Green (555nm)" package="3 mm [THT]"]
  LED2 = LED - 3mm [color="Green (555nm)" package="3 mm [THT]"]
  LED3 = LED - 3mm [color="Green (555nm)" package="3 mm [THT]"]
  LED4 = LED - 3mm [color="Green (555nm)" package="3 mm [THT]"]
  R2 = Resistor [tolerance=±5% resistance=220 package=THT]
  R3 = Resistor [tolerance=±5% resistance=220 package=THT]
  R4 = Resistor [tolerance=±5% resistance=220 package=THT]
  R5 = Resistor [tolerance=±5% resistance=220 package="0402 [SMD]"]
  HC-SR04_Sensor_1 = HC-SR04 Ultrasonic Distance Sensor
  R6 = Resistor [tolerance=±5% resistance=220 package="0603 [SMD]"]
  LCD1 = LCD screen
  U1 = POT [package=alps_pot]

nets:
  N1: Composant1.A4/SDA, HC-SR04_Sensor_1.GND
  N2: Composant1.A5/SCL, S1.2, R6.Pin_0
  N3: Composant1.D8, SG1.2
  N4: Composant1.D9_PWM, R5.Pin_0
  N5: Composant1.D10_PWM/SS, R4.Pin_0
  N6: Composant1.D11_PWM/MOSI, LCD1.E
  N7: Composant1.D12/MISO, LCD1.RS
  N8: Composant1.D13/SCK, HC-SR04_Sensor_1.TRIG
  GND: Composant1.GND, SG1.1, LED1.cathode, LED2.cathode, LED3.cathode, LED4.cathode, HC-SR04_Sensor_1.ECHO, R6.Pin_1, LCD1.VSS, LCD1.R/W, LCD1.DB0, LCD1.DB1, LCD1.DB2, LCD1.DB3, LCD1.LED-, U1.A
  N9: Composant1.D2, LCD1.DB7
  N10: Composant1.D3_PWM, LCD1.DB6
  N11: Composant1.D4, LCD1.DB5
  N12: Composant1.D5_PWM, LCD1.DB4
  N13: Composant1.D6_PWM, R2.Pin_0
  N14: Composant1.D7, R3.Pin_0
  5V: Composant1.5V, R1.Pin_0, S1.1, HC-SR04_Sensor_1.VCC, LCD1.VDD, U1.E
  N15: R1.Pin_1, LCD1.LED+
  N16: LED1.anode, R5.Pin_1
  N17: LED2.anode, R2.Pin_1
  N18: LED3.anode, R4.Pin_1
  N19: LED4.anode, R3.Pin_1
  N20: LCD1.V0, U1.S
